# Fritzing sketch IRremoto_servo (saved by Fritzing 0.9.0b)
breadboards: 1

parts:
  Parte1 = Arduino Mega 2560 (Rev3)
  J2 = Basic Servo
  J3 = Infrared Proximity Sensor

nets:
  N1: Parte1.D9_PWM, J2.pulse
  VCC: Parte1.5V, J2.vcc, J3.Vcc
  GND: Parte1.GND, J2.gnd, J3.GND
  N2: Parte1.D4_PWM, J3.Vout

notes:
  Se leia un valor el cual se convertia a entero para despues hacer comparaciones, si el boton precionado era
  para mover hacia derecha o izquierda lo hacia el servo
  Librerias <Servo.h> e <IRremote.h> facilitan el trabajo solo hay que saberlas utilizar
  Esta practica tampoco tuvo complejidad en sus conexiones, el reto era observar el funcionamiento de las librerias importadas junto con sus funciones
